# Fritzing sketch PWM-NodeMCU (saved by Fritzing 0.9.5d)
breadboards: 1

parts:
  U1 = ESP8266 NodeMCU LoLin module
  R1 = Resistor [tolerance=±5% resistance=330 package="2010 [SMD]"]
  R2 = PHOTOCELL [package=photocell]

nets:
  N1: U1.3V3, R2.P$2
  N2: U1.GND, R1.Pin_0
  N3: U1.A0, R1.Pin_1, R2.P$1

custom parts:
  ESP8266 NodeMCU LoLin module: ESP8266 based NodeMCU
